// Logisim project Project2.circ as structural Verilog: 4 circuits, main circuit MIPS32
module MIPS32 (
  input  in_1,
  input  in_2,
  input  ONOFF
);

  wire clock_1_out, mips_alu_1_p3, registerfile_1_p4, registerfile_1_p6, registerfile_1_p7, undriven,
       undriven_2;
  wire [31:0] B_q, bit_extender_1_out, CTRL_2_q, CTRL_q, D_2_q, D_q, ifid_1_qa, ifid_1_qb, ifid_1_qimm,
       incrementer4_1_out_2, M_q, mips_alu_1_p4, mipsprogramrom_1_p2, multiplexer_1_out, pc_1_o,
       register_1_q, registerfile_1_p1, registerfile_1_p5, registerfile_1_p10, registerfile_1_p11;

  PC pc_1 (.I(incrementer4_1_out_2), .WE(ONOFF), .Reset(in_1), .R(clock_1_out), .Reset2(in_2), .O(pc_1_o));
  Incrementer4 incrementer4_1 (.in_1(pc_1_o), .out_2(incrementer4_1_out_2));
  // Probe on incrementer4_1_out_2
  // MIPSProgramROM mipsprogramrom_1: pin names not known; wires that end beside it: pc_1_o, mipsprogramrom_1_p2
  Register #(.width(32)) register_1 (
    .D(mipsprogramrom_1_p2), .en(ONOFF), .clk(clock_1_out), .Q(register_1_q));  // open: clr
  Clock clock_1 (.out(clock_1_out));
  // RegisterFile registerfile_1: pin names not known; wires that end beside it: registerfile_1_p1, clock_1_out, register_1_q, registerfile_1_p4, registerfile_1_p5, registerfile_1_p6, registerfile_1_p7, registerfile_1_p6, registerfile_1_p7, registerfile_1_p10, registerfile_1_p11
  assign bit_extender_1_out = {{16{register_1_q[15]}}, register_1_q[15:0]};  // Bit_Extender bit_extender_1
  Register #(.width(32)) CTRL (.D(registerfile_1_p5), .en(ONOFF), .clk(clock_1_out), .Q(CTRL_q));  // open: clr
  IFID ifid_1 (
    .WE(ONOFF), .R(clock_1_out), .DA(registerfile_1_p10), .DB(registerfile_1_p11), .DIMM(bit_extender_1_out),
    .QA(ifid_1_qa), .QB(ifid_1_qb), .QIMM(ifid_1_qimm));
  Multiplexer #(.width(32), .enable("false")) multiplexer_1 (
    .in0(ifid_1_qb), .in1(ifid_1_qimm), .out(multiplexer_1_out), .sel(undriven));
  // Mips_ALU mips_alu_1: pin names not known; wires that end beside it: ifid_1_qa, multiplexer_1_out, mips_alu_1_p3, mips_alu_1_p4
  Register #(.width(32)) D (.D(mips_alu_1_p4), .en(ONOFF), .clk(clock_1_out), .Q(D_q));  // open: clr
  Register #(.width(32)) B (.D(ifid_1_qb), .en(ONOFF), .clk(clock_1_out), .Q(B_q));  // open: clr
  Register #(.width(32)) CTRL_2 (.D(CTRL_q), .en(ONOFF), .clk(clock_1_out), .Q(CTRL_2_q));  // open: clr
  Register #(.width(32)) D_2 (.D(D_q), .en(ONOFF), .clk(clock_1_out), .Q(D_2_q));  // open: clr
  Register #(.width(32)) M (.D(B_q), .en(ONOFF), .clk(clock_1_out), .Q(M_q));  // open: clr
  Register #(.width(32)) CTRL_3 (.D(CTRL_2_q), .en(ONOFF), .clk(clock_1_out));  // open: Q, clr
  Multiplexer #(.width(32), .enable("false")) multiplexer_2 (
    .in0(D_2_q), .in1(M_q), .out(registerfile_1_p1), .sel(undriven_2));

  // Notes on the sheet:
  //   Data?
  //   Write Enabled
  //   Decode
  //   SELECTORS
endmodule

module Incrementer4 (
  input  [31:0] in_1,
  output [31:0] out_2
);

  wire incrementer_1_p2, incrementer_2_p2, incrementer_3_p2;

  // Incrementer #(.width(32)) incrementer_1: pin names not known; wires that end beside it: in_1, incrementer_1_p2
  // Incrementer #(.width(32)) incrementer_2: pin names not known; wires that end beside it: incrementer_1_p2, incrementer_2_p2
  // Incrementer #(.width(32)) incrementer_3: pin names not known; wires that end beside it: incrementer_2_p2, incrementer_3_p2
  // Incrementer #(.width(32)) incrementer_4: pin names not known; wires that end beside it: incrementer_3_p2, out_2
endmodule

module PC (
  input  [31:0] I,
  input  WE,
  input  Reset,
  input  R,
  input  Reset2,
  output [31:0] O
);

  wire not_1_out, or_1_out;
  wire [31:0] multiplexer_1_out;

  Multiplexer #(.width(32), .enable("false")) multiplexer_1 (
    .in0({32{1'b0}}), .in1(I), .out(multiplexer_1_out), .sel(not_1_out));
  not not_1 (not_1_out, Reset);
  or or_1 (or_1_out, R, Reset2);
  Register #(.width(32)) register_1 (.D(multiplexer_1_out), .en(WE), .clk(or_1_out), .Q(O));  // open: clr
endmodule

module IFID (
  input  WE,
  input  R,
  input  [31:0] DA,
  input  [31:0] DB,
  input  [31:0] DIMM,
  output [31:0] QA,
  output [31:0] QB,
  output [31:0] QIMM
);

  Register #(.width(32)) register_1 (.D(DA), .en(WE), .clk(R), .Q(QA));  // open: clr
  Register #(.width(32)) register_2 (.D(DB), .en(WE), .clk(R), .Q(QB));  // open: clr
  Register #(.width(32)) register_3 (.D(DIMM), .en(WE), .clk(R), .Q(QIMM));  // open: clr
endmodule
